// Logisim project memoria.circ as structural Verilog: 8 circuits, main circuit main
module main (
);

  wire Coluna, Confirma, Jogador_1, Jogador_2, L11, L12, L13, L14, L21, L22, L23, L24, L31, L32, L33, L34,
       L41, L42, L43, L44, Linha;
  wire [3:0] Pont_1, Pont_2, V11, V12, V13, V14, V21, V22, V23, V24, V31, V32, V33, V34, V41, V42, V43, V44;

  LED led_1 (.in(Jogador_1));
  Hex_Digit_Display hex_digit_display_1 (.value(Pont_1));  // open: dp
  control_L_C control_l_c_1 (
    .in_1(Linha), .in_2(Coluna), .L11(L11), .L12(L12), .L13(L13), .L14(L14), .L21(L21), .L22(L22), .L23(L23),
    .L24(L24), .L31(L31), .L32(L32), .L33(L33), .L34(L34), .L41(L41), .L42(L42), .L43(L43), .L44(L44));
  LED led_2 (.in(L11));
  Hex_Digit_Display hex_digit_display_2 (.value(V11));  // open: dp
  LED led_3 (.in(L21));
  Hex_Digit_Display hex_digit_display_3 (.value(V21));  // open: dp
  LED led_4 (.in(L31));
  Hex_Digit_Display hex_digit_display_4 (.value(V31));  // open: dp
  LED led_5 (.in(L41));
  Hex_Digit_Display hex_digit_display_5 (.value(V41));  // open: dp
  Button button_1 (.out(Linha));
  LED led_6 (.in(L12));
  Hex_Digit_Display hex_digit_display_6 (.value(V12));  // open: dp
  LED led_7 (.in(L22));
  Hex_Digit_Display hex_digit_display_7 (.value(V22));  // open: dp
  LED led_8 (.in(L32));
  Hex_Digit_Display hex_digit_display_8 (.value(V32));  // open: dp
  LED led_9 (.in(L42));
  Hex_Digit_Display hex_digit_display_9 (.value(V42));  // open: dp
  Button button_2 (.out(Coluna));
  Button button_3 (.out(Confirma));
  LED led_10 (.in(L13));
  Hex_Digit_Display hex_digit_display_10 (.value(V13));  // open: dp
  LED led_11 (.in(L23));
  Hex_Digit_Display hex_digit_display_11 (.value(V23));  // open: dp
  LED led_12 (.in(L33));
  Hex_Digit_Display hex_digit_display_12 (.value(V33));  // open: dp
  LED led_13 (.in(L43));
  Hex_Digit_Display hex_digit_display_13 (.value(V43));  // open: dp
  LED led_14 (.in(L14));
  Hex_Digit_Display hex_digit_display_14 (.value(V14));  // open: dp
  LED led_15 (.in(L24));
  Hex_Digit_Display hex_digit_display_15 (.value(V24));  // open: dp
  LED led_16 (.in(L34));
  Hex_Digit_Display hex_digit_display_16 (.value(V34));  // open: dp
  LED led_17 (.in(L44));
  Hex_Digit_Display hex_digit_display_17 (.value(V44));  // open: dp
  LED led_18 (.in(Jogador_2));
  Hex_Digit_Display hex_digit_display_18 (.value(Pont_2));  // open: dp
  Mux_rev mux_rev_1 (
    .Confirma(Confirma), .L11(L11), .L12(L12), .L13(L13), .L14(L14), .L21(L21), .L22(L22), .L23(L23),
    .L24(L24), .L31(L31), .L32(L32), .L33(L33), .L34(L34), .L41(L41), .L42(L42), .L43(L43), .L43_2(L44),
    .L11_2(V11), .L12_2(V12), .L13_2(V13), .L14_2(V14), .L21_2(V21), .L22_2(V22), .L23_2(V23), .L24_2(V24),
    .L31_2(V31), .L32_2(V32), .L33_2(V33), .L34_2(V34), .L41_2(V41), .L42_2(V42), .L43_3(V43), .L44(V44),
    .J1(Jogador_1), .J2(Jogador_2), .P1(Pont_1), .P2(Pont_2));
endmodule

module Mux_rev (
  input  Confirma,
  input  L11,
  input  L12,
  input  L13,
  input  L14,
  input  L21,
  input  L22,
  input  L23,
  input  L24,
  input  L31,
  input  L32,
  input  L33,
  input  L34,
  input  L41,
  input  L42,
  input  L43,
  input  L43_2,
  output [3:0] L11_2,
  output [3:0] L12_2,
  output [3:0] L13_2,
  output [3:0] L14_2,
  output [3:0] L21_2,
  output [3:0] L22_2,
  output [3:0] L23_2,
  output [3:0] L24_2,
  output [3:0] L31_2,
  output [3:0] L32_2,
  output [3:0] L33_2,
  output [3:0] L34_2,
  output [3:0] L41_2,
  output [3:0] L42_2,
  output [3:0] L43_3,
  output [3:0] L44,
  output J1,
  output J2,
  output [3:0] P1,
  output [3:0] P2
);

  wire and_3_out, and_4_out, and_5_out, and_6_out, and_7_out, and_8_out, and_9_out, and_10_out, Certo_1,
       Certo_2, Certo_3, Certo_4, Certo_5, Certo_6, Certo_7, Certo_8, Confirm, Mux11, Mux12, Mux13, Mux14,
       Mux21, Mux22, Mux23, Mux24, Mux31, Mux32, Mux33, Mux34, Mux41, Mux42, Mux43, Mux44, or_1_out,
       or_2_out, or_3_out, or_4_out, or_5_out, or_6_out, or_7_out, or_8_out, or_9_out, or_10_out, or_11_out,
       or_12_out, or_13_out, or_14_out, or_15_out, or_16_out, or_17_out, Reset;
  wire [1:0] incrementa_1_out_3;

  and and_1 (Confirm, Confirma, or_5_out);
  D_Flip_Flop #(.Pre_Clr_Positions("LEGACY"), .enable("true"), .NewFFLayout("false")) d_ff_1 (
    .clk(Confirm), .D(L11), .Q(Mux11), .preset(or_1_out), .reset(Reset));  // open: Qn, en
  or or_1 (or_1_out, Certo_1, Mux11);
  D_Flip_Flop #(.Pre_Clr_Positions("LEGACY"), .enable("true"), .NewFFLayout("false")) d_ff_2 (
    .clk(Confirm), .D(L21), .Q(Mux21), .preset(or_2_out), .reset(Reset));  // open: Qn, en
  or or_2 (or_2_out, Certo_4, Mux21);
  D_Flip_Flop #(.Pre_Clr_Positions("LEGACY"), .enable("true"), .NewFFLayout("false")) d_ff_3 (
    .clk(Confirm), .D(L31), .Q(Mux31), .preset(or_3_out), .reset(Reset));  // open: Qn, en
  or or_3 (or_3_out, Certo_6, Mux31);
  D_Flip_Flop #(.Pre_Clr_Positions("LEGACY"), .enable("true"), .NewFFLayout("false")) d_ff_4 (
    .clk(Confirm), .D(L41), .Q(Mux41), .preset(or_4_out), .reset(Reset));  // open: Qn, en
  or or_4 (or_4_out, Certo_7, Mux41);
  or or_5 (or_5_out, incrementa_1_out_3[1], incrementa_1_out_3[0]);
  incrementa incrementa_1 (.in_1(Confirma), .in_2(Reset), .out_3(incrementa_1_out_3));
  Multiplexer #(.width(4), .enable("false")) multiplexer_1 (.in1(4'b0001), .out(L11_2), .sel(Mux11));  // open: in0
  Multiplexer #(.width(4), .enable("false")) multiplexer_2 (.in1(4'b0010), .out(L21_2), .sel(Mux21));  // open: in0
  Multiplexer #(.width(4), .enable("false")) multiplexer_3 (.in1(4'b0011), .out(L31_2), .sel(Mux31));  // open: in0
  Multiplexer #(.width(4), .enable("false")) multiplexer_4 (.in1(4'b0100), .out(L41_2), .sel(Mux41));  // open: in0
  and and_2 (Reset, incrementa_1_out_3[0], incrementa_1_out_3[1]);
  D_Flip_Flop #(.Pre_Clr_Positions("LEGACY"), .enable("true"), .NewFFLayout("false")) d_ff_5 (
    .clk(Confirm), .D(L12), .Q(Mux12), .preset(or_6_out), .reset(Reset));  // open: Qn, en
  or or_6 (or_6_out, Certo_2, Mux12);
  D_Flip_Flop #(.Pre_Clr_Positions("LEGACY"), .enable("true"), .NewFFLayout("false")) d_ff_6 (
    .clk(Confirm), .D(L22), .Q(Mux22), .preset(or_7_out), .reset(Reset));  // open: Qn, en
  or or_7 (or_7_out, Certo_5, Mux22);
  D_Flip_Flop #(.Pre_Clr_Positions("LEGACY"), .enable("true"), .NewFFLayout("false")) d_ff_7 (
    .clk(Confirm), .D(L32), .Q(Mux32), .preset(or_8_out), .reset(Reset));  // open: Qn, en
  or or_8 (or_8_out, Certo_7, Mux32);
  D_Flip_Flop #(.Pre_Clr_Positions("LEGACY"), .enable("true"), .NewFFLayout("false")) d_ff_8 (
    .clk(Confirm), .D(L42), .Q(Mux42), .preset(or_9_out), .reset(Reset));  // open: Qn, en
  or or_9 (or_9_out, Certo_8, Mux42);
  and and_3 (and_3_out, Mux11, Mux14);
  and and_4 (and_4_out, Mux33, Mux12);
  and and_5 (and_5_out, Mux13, Mux23);
  Multiplexer #(.width(4), .enable("false")) multiplexer_5 (.in1(4'b0111), .out(L12_2), .sel(Mux12));  // open: in0
  Multiplexer #(.width(4), .enable("false")) multiplexer_6 (.in1(4'b0110), .out(L22_2), .sel(Mux22));  // open: in0
  Multiplexer #(.width(4), .enable("false")) multiplexer_7 (.in1(4'b0100), .out(L32_2), .sel(Mux32));  // open: in0
  Multiplexer #(.width(4), .enable("false")) multiplexer_8 (.in1(4'b1000), .out(L42_2), .sel(Mux42));  // open: in0
  D_Flip_Flop #(.Pre_Clr_Positions("LEGACY"), .enable("true"), .NewFFLayout("false")) d_ff_9 (
    .clk(and_3_out), .D(and_3_out), .Q(Certo_1));  // open: Qn, preset, en, reset
  D_Flip_Flop #(.Pre_Clr_Positions("LEGACY"), .enable("true"), .NewFFLayout("false")) d_ff_10 (
    .clk(and_4_out), .D(and_4_out), .Q(Certo_2));  // open: Qn, preset, en, reset
  D_Flip_Flop #(.Pre_Clr_Positions("LEGACY"), .enable("true"), .NewFFLayout("false")) d_ff_11 (
    .clk(and_5_out), .D(and_5_out), .Q(Certo_3));  // open: Qn, preset, en, reset
  D_Flip_Flop #(.Pre_Clr_Positions("LEGACY"), .enable("true"), .NewFFLayout("false")) d_ff_12 (
    .clk(Confirm), .D(L13), .Q(Mux13), .preset(or_10_out), .reset(Reset));  // open: Qn, en
  or or_10 (or_10_out, Certo_3, Mux13);
  D_Flip_Flop #(.Pre_Clr_Positions("LEGACY"), .enable("true"), .NewFFLayout("false")) d_ff_13 (
    .clk(Confirm), .D(L23), .Q(Mux23), .preset(or_11_out), .reset(Reset));  // open: Qn, en
  or or_11 (or_11_out, Certo_3, Mux23);
  or or_12 (or_12_out, Certo_2, Mux33);
  or or_13 (or_13_out, Certo_6, Mux43);
  D_Flip_Flop #(.Pre_Clr_Positions("LEGACY"), .enable("true"), .NewFFLayout("false")) d_ff_14 (
    .clk(and_6_out), .D(and_6_out), .Q(Certo_4));  // open: Qn, preset, en, reset
  and and_6 (and_6_out, Mux21, Mux24);
  and and_7 (and_7_out, Mux22, Mux34);
  D_Flip_Flop #(.Pre_Clr_Positions("LEGACY"), .enable("true"), .NewFFLayout("false")) d_ff_15 (
    .clk(and_7_out), .D(and_7_out), .Q(Certo_5));  // open: Qn, preset, en, reset
  and and_8 (and_8_out, Mux31, Mux43);
  D_Flip_Flop #(.Pre_Clr_Positions("LEGACY"), .enable("true"), .NewFFLayout("false")) d_ff_16 (
    .clk(and_8_out), .D(and_8_out), .Q(Certo_6));  // open: Qn, preset, en, reset
  Multiplexer #(.width(4), .enable("false")) multiplexer_9 (.in1(4'b0101), .out(L13_2), .sel(Mux13));  // open: in0
  Multiplexer #(.width(4), .enable("false")) multiplexer_10 (.in1(4'b0101), .out(L23_2), .sel(Mux23));  // open: in0
  D_Flip_Flop #(.Pre_Clr_Positions("LEGACY"), .enable("true"), .NewFFLayout("false")) d_ff_17 (
    .clk(Confirm), .D(L33), .Q(Mux33), .preset(or_12_out), .reset(Reset));  // open: Qn, en
  D_Flip_Flop #(.Pre_Clr_Positions("LEGACY"), .enable("true"), .NewFFLayout("false")) d_ff_18 (
    .clk(Confirm), .D(L43), .Q(Mux43), .preset(or_13_out), .reset(Reset));  // open: Qn, en
  Multiplexer #(.width(4), .enable("false")) multiplexer_11 (.in1(4'b0111), .out(L33_2), .sel(Mux33));  // open: in0
  Multiplexer #(.width(4), .enable("false")) multiplexer_12 (.in1(4'b0011), .out(L43_3), .sel(Mux43));  // open: in0
  and and_9 (and_9_out, Mux32, Mux41);
  and and_10 (and_10_out, Mux42, Mux44);
  or or_14 (or_14_out, Certo_1, Mux14);
  or or_15 (or_15_out, Certo_4, Mux24);
  or or_16 (or_16_out, Certo_5, Mux34);
  or or_17 (or_17_out, Certo_8, Mux44);
  D_Flip_Flop #(.Pre_Clr_Positions("LEGACY"), .enable("true"), .NewFFLayout("false")) d_ff_19 (
    .clk(and_9_out), .D(and_9_out), .Q(Certo_7));  // open: Qn, preset, en, reset
  D_Flip_Flop #(.Pre_Clr_Positions("LEGACY"), .enable("true"), .NewFFLayout("false")) d_ff_20 (
    .clk(and_10_out), .D(and_10_out), .Q(Certo_8));  // open: Qn, preset, en, reset
  D_Flip_Flop #(.Pre_Clr_Positions("LEGACY"), .enable("true"), .NewFFLayout("false")) d_ff_21 (
    .clk(Confirm), .D(L14), .Q(Mux14), .preset(or_14_out), .reset(Reset));  // open: Qn, en
  D_Flip_Flop #(.Pre_Clr_Positions("LEGACY"), .enable("true"), .NewFFLayout("false")) d_ff_22 (
    .clk(Confirm), .D(L24), .Q(Mux24), .preset(or_15_out), .reset(Reset));  // open: Qn, en
  D_Flip_Flop #(.Pre_Clr_Positions("LEGACY"), .enable("true"), .NewFFLayout("false")) d_ff_23 (
    .clk(Confirm), .D(L34), .Q(Mux34), .preset(or_16_out), .reset(Reset));  // open: Qn, en
  D_Flip_Flop #(.Pre_Clr_Positions("LEGACY"), .enable("true"), .NewFFLayout("false")) d_ff_24 (
    .clk(Confirm), .D(L43_2), .Q(Mux44), .preset(or_17_out), .reset(Reset));  // open: Qn, en
  Multiplexer #(.width(4), .enable("false")) multiplexer_13 (.in1(4'b0001), .out(L14_2), .sel(Mux14));  // open: in0
  Multiplexer #(.width(4), .enable("false")) multiplexer_14 (.in1(4'b0010), .out(L24_2), .sel(Mux24));  // open: in0
  Multiplexer #(.width(4), .enable("false")) multiplexer_15 (.in1(4'b0110), .out(L34_2), .sel(Mux34));  // open: in0
  Multiplexer #(.width(4), .enable("false")) multiplexer_16 (.in1(4'b1000), .out(L44), .sel(Mux44));  // open: in0
  Pont pont_1 (
    .in_3(Certo_1), .in_4(Certo_2), .in_5(Certo_3), .in_6(Certo_4), .in_7(Certo_5), .in_8(Certo_6),
    .in_9(Certo_7), .in_10(Certo_8), .J1(J1), .J2(J2), .out_11(P1), .out_12(P2));
  D_Flip_Flop #(.Pre_Clr_Positions("LEGACY"), .enable("true"), .NewFFLayout("false")) d_ff_25 (
    .clk(Reset), .D(J1), .Q(J2), .Qn(J1));  // open: preset, en, reset

  // Other names for the same wires on the sheet: L11_t[3:0] = L11_2; L12_t[3:0] = L12_2; L13_t[3:0] = L13_2;
  //   L14_t[3:0] = L14_2; L21_t[3:0] = L21_2; L22_t[3:0] = L22_2; L23_t[3:0] = L23_2; L24_t[3:0] = L24_2;
  //   L31_t[3:0] = L31_2; L32_t[3:0] = L32_2; L33_t[3:0] = L33_2; L34_t[3:0] = L34_2; L41_t[3:0] = L41_2;
  //   L42_t[3:0] = L42_2; L43_t[3:0] = L43_3
endmodule

module control_L_C (
  input  in_1,
  input  in_2,
  output L11,
  output L12,
  output L13,
  output L14,
  output L21,
  output L22,
  output L23,
  output L24,
  output L31,
  output L32,
  output L33,
  output L34,
  output L41,
  output L42,
  output L43,
  output L44
);

  wire not_1_out, not_2_out, not_3_out, not_4_out, not_5_out, not_6_out, not_7_out, not_8_out, not_9_out,
       not_10_out, not_11_out, not_12_out, not_13_out, not_14_out, not_15_out, not_16_out, not_17_out,
       not_18_out, not_19_out, not_20_out, not_21_out, not_22_out, not_23_out, not_24_out, not_25_out,
       not_26_out, not_27_out, not_28_out, not_29_out, not_30_out, not_31_out, not_32_out;
  wire [1:0] incrementa_1_out_3, incrementa_2_out_3;

  incrementa incrementa_1 (.in_1(in_1), .out_3(incrementa_1_out_3));  // open: in_2
  incrementa incrementa_2 (.in_1(in_2), .out_3(incrementa_2_out_3));  // open: in_2
  not not_1 (not_1_out, incrementa_1_out_3[1]);
  not not_2 (not_2_out, incrementa_1_out_3[0]);
  not not_3 (not_3_out, incrementa_2_out_3[1]);
  not not_4 (not_4_out, incrementa_2_out_3[0]);
  not not_5 (not_5_out, incrementa_1_out_3[1]);
  not not_6 (not_6_out, incrementa_1_out_3[0]);
  not not_7 (not_7_out, incrementa_2_out_3[1]);
  not not_8 (not_8_out, incrementa_1_out_3[1]);
  not not_9 (not_9_out, incrementa_1_out_3[0]);
  not not_10 (not_10_out, incrementa_2_out_3[0]);
  not not_11 (not_11_out, incrementa_1_out_3[1]);
  not not_12 (not_12_out, incrementa_1_out_3[0]);
  not not_13 (not_13_out, incrementa_1_out_3[1]);
  not not_14 (not_14_out, incrementa_2_out_3[1]);
  not not_15 (not_15_out, incrementa_2_out_3[0]);
  not not_16 (not_16_out, incrementa_1_out_3[1]);
  not not_17 (not_17_out, incrementa_2_out_3[1]);
  not not_18 (not_18_out, incrementa_1_out_3[1]);
  not not_19 (not_19_out, incrementa_2_out_3[0]);
  not not_20 (not_20_out, incrementa_1_out_3[1]);
  not not_21 (not_21_out, incrementa_1_out_3[0]);
  not not_22 (not_22_out, incrementa_2_out_3[1]);
  not not_23 (not_23_out, incrementa_2_out_3[0]);
  not not_24 (not_24_out, incrementa_1_out_3[0]);
  not not_25 (not_25_out, incrementa_2_out_3[1]);
  not not_26 (not_26_out, incrementa_1_out_3[0]);
  not not_27 (not_27_out, incrementa_2_out_3[0]);
  not not_28 (not_28_out, incrementa_1_out_3[0]);
  not not_29 (not_29_out, incrementa_2_out_3[1]);
  not not_30 (not_30_out, incrementa_2_out_3[0]);
  not not_31 (not_31_out, incrementa_2_out_3[1]);
  not not_32 (not_32_out, incrementa_2_out_3[0]);
  and and_1 (L11, not_1_out, not_2_out, not_3_out, not_4_out);
  and and_2 (L12, not_5_out, not_6_out, not_7_out, incrementa_2_out_3[0]);
  and and_3 (L13, not_8_out, not_9_out, incrementa_2_out_3[1], not_10_out);
  and and_4 (L14, not_11_out, not_12_out, incrementa_2_out_3[1], incrementa_2_out_3[0]);
  and and_5 (L21, not_13_out, incrementa_1_out_3[0], not_14_out, not_15_out);
  and and_6 (L22, not_16_out, incrementa_1_out_3[0], not_17_out, incrementa_2_out_3[0]);
  and and_7 (L23, not_18_out, incrementa_1_out_3[0], incrementa_2_out_3[1], not_19_out);
  and and_8 (L24, not_20_out, incrementa_1_out_3[0], incrementa_2_out_3[1], incrementa_2_out_3[0]);
  and and_9 (L31, incrementa_1_out_3[1], not_21_out, not_22_out, not_23_out);
  and and_10 (L32, incrementa_1_out_3[1], not_24_out, not_25_out, incrementa_2_out_3[0]);
  and and_11 (L33, incrementa_1_out_3[1], not_26_out, incrementa_2_out_3[1], not_27_out);
  and and_12 (L34, incrementa_1_out_3[1], not_28_out, incrementa_2_out_3[1], incrementa_2_out_3[0]);
  and and_13 (L41, incrementa_1_out_3[1], incrementa_1_out_3[0], not_29_out, not_30_out);
  and and_14 (L42, incrementa_1_out_3[1], incrementa_1_out_3[0], not_31_out, incrementa_2_out_3[0]);
  and and_15 (L43, incrementa_1_out_3[1], incrementa_1_out_3[0], incrementa_2_out_3[1], not_32_out);
  and and_16 (L44, incrementa_1_out_3[1], incrementa_1_out_3[0], incrementa_2_out_3[1], incrementa_2_out_3[0]);
endmodule

module incrementa (
  input  in_1,
  input  in_2,
  output [1:0] out_3
);

  wire incrementador_1_s1, incrementador_1_s2;

  D_Flip_Flop #(.Pre_Clr_Positions("LEGACY"), .enable("true"), .NewFFLayout("false")) d_ff_1 (
    .clk(in_1), .D(incrementador_1_s1), .Q(out_3[1]), .reset(in_2));  // open: Qn, preset, en
  D_Flip_Flop #(.Pre_Clr_Positions("LEGACY"), .enable("true"), .NewFFLayout("false")) d_ff_2 (
    .clk(in_1), .D(incrementador_1_s2), .Q(out_3[0]), .reset(in_2));  // open: Qn, preset, en
  incrementador incrementador_1 (.a(out_3[1]), .b(out_3[0]), .s1(incrementador_1_s1), .s2(incrementador_1_s2));
endmodule

module incrementador (
  input  a,
  input  b,
  output s1,
  output s2
);

  wire and_1_out, and_2_out, not_1_out, not_2_out;

  not not_1 (not_1_out, a);
  not not_2 (not_2_out, b);
  not not_3 (s2, b);
  and and_1 (and_1_out, not_1_out, b);
  and and_2 (and_2_out, a, not_2_out);
  or or_1 (s1, and_1_out, and_2_out);
endmodule

module Pont (
  input  J1,
  input  J2,
  input  in_3,
  input  in_4,
  input  in_5,
  input  in_6,
  input  in_7,
  input  in_8,
  input  in_9,
  input  in_10,
  output [3:0] out_11,
  output [3:0] out_12
);

  wire and_1_out, and_2_out, and_3_out, and_4_out, and_5_out, and_6_out, and_7_out, and_8_out, and_9_out,
       and_10_out, d_ff_1_q, d_ff_1_qn, d_ff_2_q, d_ff_2_qn, d_ff_3_q, d_ff_3_qn, d_ff_4_q, d_ff_4_qn,
       d_ff_5_q, d_ff_5_qn, d_ff_6_q, d_ff_6_qn, d_ff_7_q, d_ff_7_qn, d_ff_8_q, d_ff_8_qn, d_ff_9_q,
       d_ff_10_q, d_ff_11_q, d_ff_12_q, d_ff_13_q, d_ff_14_q, d_ff_15_q, d_ff_16_q, or_1_out;

  and and_1 (and_1_out, in_3, ~d_ff_9_q);  // AND_Gate
  D_Flip_Flop #(.Pre_Clr_Positions("LEGACY"), .enable("true"), .NewFFLayout("false")) d_ff_1 (
    .clk(and_1_out), .D(d_ff_1_qn), .Q(d_ff_1_q), .Qn(d_ff_1_qn), .reset(d_ff_9_q));  // open: preset, en
  D_Flip_Flop #(.Pre_Clr_Positions("LEGACY"), .enable("true"), .NewFFLayout("false")) d_ff_2 (
    .clk(and_2_out), .D(d_ff_2_qn), .Q(d_ff_2_q), .Qn(d_ff_2_qn), .reset(d_ff_10_q));  // open: preset, en
  and and_2 (and_2_out, in_4, ~d_ff_10_q);  // AND_Gate
  and and_3 (and_3_out, in_5, ~d_ff_11_q);  // AND_Gate
  D_Flip_Flop #(.Pre_Clr_Positions("LEGACY"), .enable("true"), .NewFFLayout("false")) d_ff_3 (
    .clk(and_3_out), .D(d_ff_3_qn), .Q(d_ff_3_q), .Qn(d_ff_3_qn), .reset(d_ff_11_q));  // open: preset, en
  D_Flip_Flop #(.Pre_Clr_Positions("LEGACY"), .enable("true"), .NewFFLayout("false")) d_ff_4 (
    .clk(and_4_out), .D(d_ff_4_qn), .Q(d_ff_4_q), .Qn(d_ff_4_qn), .reset(d_ff_12_q));  // open: preset, en
  and and_4 (and_4_out, in_6, ~d_ff_12_q);  // AND_Gate
  D_Flip_Flop #(.Pre_Clr_Positions("LEGACY"), .enable("true"), .NewFFLayout("false")) d_ff_5 (
    .clk(and_5_out), .D(d_ff_5_qn), .Q(d_ff_5_q), .Qn(d_ff_5_qn), .reset(d_ff_13_q));  // open: preset, en
  and and_5 (and_5_out, in_7, ~d_ff_13_q);  // AND_Gate
  D_Flip_Flop #(.Pre_Clr_Positions("LEGACY"), .enable("true"), .NewFFLayout("false")) d_ff_6 (
    .clk(and_6_out), .D(d_ff_6_qn), .Q(d_ff_6_q), .Qn(d_ff_6_qn), .reset(d_ff_14_q));  // open: preset, en
  and and_6 (and_6_out, in_8, ~d_ff_14_q);  // AND_Gate
  D_Flip_Flop #(.Pre_Clr_Positions("LEGACY"), .enable("true"), .NewFFLayout("false")) d_ff_7 (
    .clk(and_7_out), .D(d_ff_7_qn), .Q(d_ff_7_q), .Qn(d_ff_7_qn), .reset(d_ff_15_q));  // open: preset, en
  and and_7 (and_7_out, in_9, ~d_ff_15_q);  // AND_Gate
  D_Flip_Flop #(.Pre_Clr_Positions("LEGACY"), .enable("true"), .NewFFLayout("false")) d_ff_8 (
    .clk(and_8_out), .D(d_ff_8_qn), .Q(d_ff_8_q), .Qn(d_ff_8_qn), .reset(d_ff_16_q));  // open: preset, en
  and and_8 (and_8_out, in_10, ~d_ff_16_q);  // AND_Gate
  D_Flip_Flop #(.Pre_Clr_Positions("LEGACY"), .enable("true"), .NewFFLayout("false")) d_ff_9 (
    .clk(d_ff_1_q), .D(d_ff_1_q), .Q(d_ff_9_q));  // open: Qn, preset, en, reset
  D_Flip_Flop #(.Pre_Clr_Positions("LEGACY"), .enable("true"), .NewFFLayout("false")) d_ff_10 (
    .clk(d_ff_2_q), .D(d_ff_2_q), .Q(d_ff_10_q));  // open: Qn, preset, en, reset
  D_Flip_Flop #(.Pre_Clr_Positions("LEGACY"), .enable("true"), .NewFFLayout("false")) d_ff_11 (
    .clk(d_ff_3_q), .D(d_ff_3_q), .Q(d_ff_11_q));  // open: Qn, preset, en, reset
  D_Flip_Flop #(.Pre_Clr_Positions("LEGACY"), .enable("true"), .NewFFLayout("false")) d_ff_12 (
    .clk(d_ff_4_q), .D(d_ff_4_q), .Q(d_ff_12_q));  // open: Qn, preset, en, reset
  D_Flip_Flop #(.Pre_Clr_Positions("LEGACY"), .enable("true"), .NewFFLayout("false")) d_ff_13 (
    .clk(d_ff_5_q), .D(d_ff_5_q), .Q(d_ff_13_q));  // open: Qn, preset, en, reset
  D_Flip_Flop #(.Pre_Clr_Positions("LEGACY"), .enable("true"), .NewFFLayout("false")) d_ff_14 (
    .clk(d_ff_6_q), .D(d_ff_6_q), .Q(d_ff_14_q));  // open: Qn, preset, en, reset
  D_Flip_Flop #(.Pre_Clr_Positions("LEGACY"), .enable("true"), .NewFFLayout("false")) d_ff_15 (
    .clk(d_ff_7_q), .D(d_ff_7_q), .Q(d_ff_15_q));  // open: Qn, preset, en, reset
  D_Flip_Flop #(.Pre_Clr_Positions("LEGACY"), .enable("true"), .NewFFLayout("false")) d_ff_16 (
    .clk(d_ff_8_q), .D(d_ff_8_q), .Q(d_ff_16_q));  // open: Qn, preset, en, reset
  or or_1 (or_1_out, d_ff_1_q, d_ff_2_q, d_ff_3_q, d_ff_4_q, d_ff_5_q, d_ff_6_q, d_ff_7_q, d_ff_8_q);
  inc_pont inc_pont_1 (.in_1(and_9_out), .out_3(out_11));  // open: in_2
  and and_9 (and_9_out, or_1_out, J1);
  and and_10 (and_10_out, or_1_out, J2);
  inc_pont inc_pont_2 (.in_1(and_10_out), .out_3(out_12));  // open: in_2
endmodule

module inc_pont (
  input  in_1,
  input  in_2,
  output [3:0] out_3
);

  wire incrementador_pont_1_s1, incrementador_pont_1_s2, incrementador_pont_1_s3, incrementador_pont_1_s4;

  D_Flip_Flop #(.Pre_Clr_Positions("LEGACY"), .enable("true"), .NewFFLayout("false")) d_ff_1 (
    .clk(in_1), .D(incrementador_pont_1_s1), .Q(out_3[3]), .reset(in_2));  // open: Qn, preset, en
  D_Flip_Flop #(.Pre_Clr_Positions("LEGACY"), .enable("true"), .NewFFLayout("false")) d_ff_2 (
    .clk(in_1), .D(incrementador_pont_1_s2), .Q(out_3[2]), .reset(in_2));  // open: Qn, preset, en
  D_Flip_Flop #(.Pre_Clr_Positions("LEGACY"), .enable("true"), .NewFFLayout("false")) d_ff_3 (
    .clk(in_1), .D(incrementador_pont_1_s3), .Q(out_3[1]), .reset(in_2));  // open: Qn, preset, en
  D_Flip_Flop #(.Pre_Clr_Positions("LEGACY"), .enable("true"), .NewFFLayout("false")) d_ff_4 (
    .clk(in_1), .D(incrementador_pont_1_s4), .Q(out_3[0]), .reset(in_2));  // open: Qn, preset, en
  incrementador_pont incrementador_pont_1 (
    .a(out_3[3]), .b(out_3[2]), .c(out_3[1]), .d(out_3[0]), .s1(incrementador_pont_1_s1),
    .s2(incrementador_pont_1_s2), .s3(incrementador_pont_1_s3), .s4(incrementador_pont_1_s4));
endmodule

module incrementador_pont (
  input  a,
  input  b,
  input  c,
  input  d,
  output s1,
  output s2,
  output s3,
  output s4
);

  wire and_1_out, and_2_out, and_3_out, and_4_out, and_5_out, and_7_out, and_8_out, not_1_out, not_2_out,
       not_3_out, not_4_out, not_5_out, not_6_out, not_7_out, not_8_out, not_9_out, not_10_out;

  not not_1 (not_1_out, a);
  not not_2 (not_2_out, b);
  not not_3 (not_3_out, c);
  not not_4 (not_4_out, b);
  and and_1 (and_1_out, not_4_out, c, d);
  and and_2 (and_2_out, b, not_5_out);
  not not_5 (not_5_out, c);
  and and_3 (and_3_out, b, not_6_out);
  not not_6 (not_6_out, d);
  not not_7 (not_7_out, c);
  and and_4 (and_4_out, not_7_out, d);
  and and_5 (and_5_out, c, not_8_out);
  not not_8 (not_8_out, d);
  not not_9 (not_9_out, a);
  and and_6 (s4, not_9_out, not_10_out);
  not not_10 (not_10_out, d);
  and and_7 (and_7_out, not_1_out, b, c, d);
  or or_1 (s1, and_7_out, and_8_out);
  and and_8 (and_8_out, a, not_2_out, not_3_out, d);
  or or_2 (s2, and_1_out, and_2_out, and_3_out);
  or or_3 (s3, and_4_out, and_5_out);
endmodule
